# Fritzing sketch TPBenito-Theremin (saved by Fritzing 0.9.4)
breadboards: 1

parts:
  Componente1 = Arduino Uno (Rev3)
  R1 = Resistor [tolerance=±5% resistance=1k package=THT]
  R2 = Resistor [tolerance=±5% resistance=1k package=THT]
  R3 = Resistor [tolerance=±5% resistance=1k package=THT]
  R4 = Resistor [tolerance=±5% resistance=1k package=THT]
  R5 = Resistor [tolerance=±5% resistance=1k package=THT]
  R6 = Resistor [tolerance=±5% resistance=1k package=THT]
  R7 = Resistor [tolerance=±5% resistance=1k package=THT]
  U1 = 7-SEGMENT-DISPLAY-1_-RED [package=7-segment-1_pth]
  HC-SR04_Sensor_1 = HC-SR04 Ultrasonic Distance Sensor
  S1 = Square Pushbutton
  S2 = Square Pushbutton
  TRS1 = Audio Jack (TRS) 3.5mm [package="PG203J [THT]"]

nets:
  N1: Componente1.D8, R7.Pin_0
  N2: Componente1.D9_PWM, TRS1.Ring
  N3: Componente1.D10_PWM/SS, S1.leg1
  N4: Componente1.D11_PWM/MOSI, S2.leg1
  N5: Componente1.D12/MISO, HC-SR04_Sensor_1.ECHO
  N6: Componente1.D13/SCK, HC-SR04_Sensor_1.TRIG
  GND: Componente1.GND, U1.G1, HC-SR04_Sensor_1.GND, S1.leg0, S2.leg0, TRS1.Sleeve
  N7: Componente1.D2, R1.Pin_0
  N8: Componente1.D3_PWM, R3.Pin_0
  N9: Componente1.D4, R2.Pin_0
  N10: Componente1.D5_PWM, R4.Pin_0
  N11: Componente1.D6_PWM, R5.Pin_0
  N12: Componente1.D7, R6.Pin_0
  5V: Componente1.5V, HC-SR04_Sensor_1.VCC
  N13: R1.Pin_1, U1.E
  N14: R2.Pin_1, U1.C
  N15: R3.Pin_1, U1.D
  N16: R4.Pin_1, U1.B
  N17: R5.Pin_1, U1.A
  N18: R6.Pin_1, U1.F
  N19: R7.Pin_1, U1.G
